# Fritzing sketch touch-lamp (saved by Fritzing 0.9.3b)
circuit board: 8.46667cm x 5.64444cm
stripboards: 1

parts:
  U1 = atmega328 [package=dip]
  CONN1 = USB connector [package=THT]
  22pF = Capacitor [package=cap-pth-small2]
  22pF_2 = Capacitor [package=cap-pth-small2]
  XTAL1 = Crystal [frequency="16 Mhz" package=SMD]
  U2 = CAPSENSE_PAD [package=capsense_pad]
  R1 = Resistor [tolerance=±5% resistance=1M package="0402 [SMD]"]
  U3 = RELAY [package=relay-g5q]

nets:
  N1: U1.D2, U3.COIL2
  VCC: U1.VCC, CONN1.5V
  N2: U1.GND#7, CONN1.GND, CONN1.chassis5, CONN1.chassis6, 22pF.1, 22pF_2.2, U3.COIL1
  N3: U1.XLAT1, 22pF.2, XTAL1.pin_0
  N4: U1.XLAT2, 22pF_2.1, XTAL1.pin_1
  N5: U1.D9_(PWM), U2.RES, R1.Pin_1
  N6: U1.D13, R1.Pin_0
